// Digital circuit 8bit-processor-dig (1).dig as structural Verilog
module _8bit_processor_dig__1 (
  input  [1:0] IR_ctrl,
  input  [1:0] Mem_ctrl,
  input  [3:0] Mem_input,
  input  [1:0] pc_ctrl,
  input  clk,
  output [3:0] PC_Output,
  output [15:0] Intructions_16_bit
);

  wire register_file_1_p4, register_file_1_p7, register_file_1_p8;
  wire [7:0] register_file_write_ctrl_1_write;

  data_path_4_bit_processor data_path_4_bit_processor_1 (
    .IR_ctrl(IR_ctrl), .PC_ctrl(pc_ctrl), .instr_mem_ctrl(Mem_ctrl), .instr_mem_input(Mem_input), .CLK(clk),
    .out(Intructions_16_bit), .PC_out(PC_Output));
  register_file_write_ctrl register_file_write_ctrl_1 (
    .Opcode_3(Intructions_16_bit[1:0]), .write(register_file_write_ctrl_1_write));
  // register_file register_file_1: pin names not known; wires that end beside it: Intructions_16_bit[5:4], Intructions_16_bit[3:2], clk, register_file_1_p4, Intructions_16_bit[1:0], register_file_write_ctrl_1_write, register_file_1_p7, register_file_1_p8
  // ALU__2 alu__2_1: pin names not known; wires that end beside it: register_file_1_p7, register_file_1_p8, Intructions_16_bit[8:6], register_file_1_p4
endmodule
