// Digital circuit register-file-write-ctrl.dig as structural Verilog
module register_file_write_ctrl (
  input  [1:0] Opcode_3,
  output [7:0] write
);

  Decoder #(.Selector_Bits(2)) decoder_1 (
    .sel(Opcode_3), .out_0(write[0]), .out_1(write[2]), .out_2(write[4]), .out_3(write[6]));

  assign {write[7], write[5], write[3], write[1]} = 4'b0000;
endmodule
